# Fritzing sketch AR05,09-프릿지 (saved by Fritzing 0.9.3b)
breadboards: 2

parts:
  부품1 = Arduino Uno (Rev3)
  J1 = Piezo Speaker
  S1 = Pushbutton [package="[THT]"]
  S2 = Pushbutton [package="[THT]"]
  부품2 = Breakout Board for Electret Microphone
  LED1 = smd LED [color="Green (570nm)" package="0805 [SMD]"]
  LED2 = smd LED [color="Yellow (595nm)" package="0805 [SMD]"]
  LED3 = smd LED [color="Red (633nm)" package="0805 [SMD]"]
  LCD1 = LCD screen  # not connected

nets:
  N1: 부품1.D9_PWM, LED2.anode
  N2: 부품1.D10_PWM/SS, LED1.anode
  N3: 부품1.D12/MISO, J1.pin2
  N4: 부품1.D2, S2.Pin_3, S2.Pin_4
  N5: 부품1.D3_PWM, S1.Pin_3, S1.Pin_4
  N6: 부품1.D5_PWM, LED3.cathode
  N7: 부품1.D6_PWM, 부품2.AUD
  5V: 부품1.5V, 부품2.VCC
  GND: 부품1.GND, J1.pin1, S1.Pin_1, S1.Pin_2, S2.Pin_1, S2.Pin_2, 부품2.GND, LED1.cathode, LED2.cathode, LED3.anode
